// Logisim project combinacionales.circ as structural Verilog: 13 circuits, main circuit verificador
module sumador_simple (
  input  A,
  input  B,
  output S,
  output Cout
);

  xor xor_1 (S, A, B);
  and and_1 (Cout, A, B);
endmodule

module sumador_completo (
  input  Cin,
  input  A,
  input  B,
  output S,
  output Cout
);

  wire sumador_simple_1_cout, sumador_simple_1_s, sumador_simple_2_cout;

  sumador_simple sumador_simple_1 (.A(A), .B(B), .S(sumador_simple_1_s), .Cout(sumador_simple_1_cout));
  sumador_simple sumador_simple_2 (.A(Cin), .B(sumador_simple_1_s), .S(S), .Cout(sumador_simple_2_cout));
  or or_1 (Cout, sumador_simple_2_cout, sumador_simple_1_cout);
endmodule

module sumador_4 (
  input  Cin,
  input  [3:0] A,
  input  [3:0] B,
  output [3:0] S,
  output Cout
);

  wire sumador_completo_1_cout, sumador_completo_2_cout, sumador_completo_3_cout;

  sumador_completo sumador_completo_1 (.Cin(Cin), .A(A[0]), .B(B[0]), .S(S[0]), .Cout(sumador_completo_1_cout));
  sumador_completo sumador_completo_2 (
    .Cin(sumador_completo_1_cout), .A(A[1]), .B(B[1]), .S(S[1]), .Cout(sumador_completo_2_cout));
  sumador_completo sumador_completo_3 (
    .Cin(sumador_completo_2_cout), .A(A[2]), .B(B[2]), .S(S[2]), .Cout(sumador_completo_3_cout));
  sumador_completo sumador_completo_4 (.Cin(sumador_completo_3_cout), .A(A[3]), .B(B[3]), .S(S[3]), .Cout(Cout));
  Hex_Digit_Display hex_digit_display_1 (.value(S));  // open: dp
endmodule

module comparador_cero (
  input  [3:0] A,
  output Z
);

  nor nor_1 (Z, A[0], A[1], A[2], A[3]);
endmodule

module sumador_flags (
  input  Cin,
  input  [3:0] A,
  input  [3:0] B,
  output [3:0] S,
  output N,
  output Z,
  output V,
  output C
);

  sumador_4 sumador_4_1 (.Cin(Cin), .A(A), .B(B), .S({N, S[2:0]}), .Cout(C));
  Hex_Digit_Display hex_digit_display_1 (.value({N, S[2:0]}));  // open: dp
  comparador_cero comparador_cero_1 (.A({N, S[2:0]}), .Z(Z));
  comp_overflow comp_overflow_1 (.c3(N), .a3(A[3]), .b3(B[3]), .O(V));

  assign S[3] = N;
endmodule

module incrementador_4 (
  input  [3:0] A,
  output [3:0] S
);

  sumador_4 sumador_4_1 (.A(A), .B(4'b0001), .S(S));  // open: Cin, Cout
  Hex_Digit_Display hex_digit_display_1 (.value(S));  // open: dp
endmodule

module inversor_4 (
  input  [3:0] A,
  input  INV,
  output [3:0] S
);

  wire [3:0] incrementador_4_1_s, not_1_out;

  not not_1 (not_1_out[0], A[0]);
  not not_2 (not_1_out[1], A[1]);
  not not_3 (not_1_out[2], A[2]);
  not not_4 (not_1_out[3], A[3]);
  Multiplexer #(.width(4)) multiplexer_1 (.in0(A), .in1(incrementador_4_1_s), .out(S), .sel(INV));
  incrementador_4 incrementador_4_1 (.A(not_1_out), .S(incrementador_4_1_s));
  Hex_Digit_Display hex_digit_display_1 (.value(S));  // open: dp
endmodule

module ALU (
  input  [3:0] A,
  input  [3:0] B,
  input  [1:0] OP,
  output N,
  output Z,
  output V,
  output C,
  output [3:0] S
);

  wire and_1_out, and_2_out, and_3_out, and_4_out, and_5_out, comparador_cero_1_z, comparador_cero_2_z,
       comparador_cero_3_z, not_1_out, not_2_out, OP_00, OP_01, OP_10, OP_11, or_2_out, or_4_out, or_5_out,
       overflow_resta_1_v_out, sumador_flags_1_c, sumador_flags_1_n, sumador_flags_1_v, sumador_flags_1_z;
  wire [3:0] inversor_4_1_s, S_and, S_or, S_t;

  Decoder #(.enable("false"), .select(2)) decoder_1 (.out0(OP_00), .out1(OP_01), .out2(OP_10), .out3(OP_11), .sel(OP));
  comparador_and comparador_and_1 (.A(A), .B(B), .Enable_out(OP_10), .S(S_and));
  comparador_or comparador_or_1 (.A(A), .B(B), .Enable_out(OP_11), .S(S_or));
  inversor_4 inversor_4_1 (.A(B), .INV(OP_01), .S(inversor_4_1_s));
  sumador_flags sumador_flags_1 (
    .Cin(1'b0), .A(A), .B(inversor_4_1_s), .S(S_t), .N(sumador_flags_1_n), .Z(sumador_flags_1_z),
    .V(sumador_flags_1_v), .C(sumador_flags_1_c));
  comparador_cero comparador_cero_1 (.A(B), .Z(comparador_cero_1_z));
  and and_1 (and_1_out, sumador_flags_1_c, OP_00);
  not not_1 (not_1_out, sumador_flags_1_c);
  not not_2 (not_2_out, comparador_cero_1_z);
  and and_2 (and_2_out, sumador_flags_1_v, OP_00);
  overflow_resta overflow_resta_1 (.V_in(sumador_flags_1_v), .B(B), .V_out(overflow_resta_1_v_out));
  and and_3 (and_3_out, not_1_out, OP_01);
  and and_4 (and_4_out, overflow_resta_1_v_out, OP_01);
  or or_1 (C, and_1_out, and_5_out);
  and and_5 (and_5_out, and_3_out, not_2_out);
  assign N = or_2_out ? sumador_flags_1_n : 1'bz;  // Controlled_Buffer controlled_buffer_1
  or or_2 (or_2_out, OP_00, OP_01);
  or or_3 (V, and_2_out, and_4_out);
  assign N = OP_11 ? S_or[3] : 1'bz;  // Controlled_Buffer controlled_buffer_2
  assign N = OP_10 ? S_and[3] : 1'bz;  // Controlled_Buffer controlled_buffer_3
  assign S = or_4_out ? S_t : 4'bz;  // Controlled_Buffer controlled_buffer_4
  or or_4 (or_4_out, OP_00, OP_01);
  assign S = OP_11 ? S_or : 4'bz;  // Controlled_Buffer controlled_buffer_5
  assign S = OP_10 ? S_and : 4'bz;  // Controlled_Buffer controlled_buffer_6
  assign Z = or_5_out ? sumador_flags_1_z : 1'bz;  // Controlled_Buffer controlled_buffer_7
  or or_5 (or_5_out, OP_00, OP_01);
  Hex_Digit_Display hex_digit_display_1 (.value(S));  // open: dp
  comparador_cero comparador_cero_2 (.A(S_or), .Z(comparador_cero_2_z));
  assign Z = OP_11 ? comparador_cero_2_z : 1'bz;  // Controlled_Buffer controlled_buffer_8
  assign Z = OP_10 ? comparador_cero_3_z : 1'bz;  // Controlled_Buffer controlled_buffer_9
  comparador_cero comparador_cero_3 (.A(S_and), .Z(comparador_cero_3_z));
endmodule

module verificador (
  output [3:0] out_1,
  output [3:0] out_2,
  output [1:0] out_3,
  output halt,
  output N,
  output Z,
  output V,
  output C,
  output [3:0] res
);

  wire clock_1_out;

  Clock clock_1 (.out(clock_1_out));
  Counter #(.max('h3ff), .width(10)) counter_1 (
    .clk(clock_1_out), .carry(halt), .Q({out_3, out_2, out_1}));  // open: clr, load, up, count, D
  ALU alu_1 (.A(out_1), .B(out_2), .OP(out_3), .N(N), .Z(Z), .V(V), .C(C), .S(res));
endmodule

module overflow_resta (
  input  V_in,
  input  [3:0] B,
  output V_out
);

  wire comparador_cero_1_z, not_2_out;
  wire [3:3] not_1_out;

  not not_1 (not_1_out[3], B[3]);
  not not_2 (not_2_out, V_in);
  comparador_cero comparador_cero_1 (.A({not_1_out[3], B[2:0]}), .Z(comparador_cero_1_z));
  Multiplexer multiplexer_1 (.in0(V_in), .in1(not_2_out), .out(V_out), .sel(comparador_cero_1_z));
endmodule

module comp_overflow (
  input  c3,
  input  a3,
  input  b3,
  output O
);

  wire not_1_out, xor_1_out, xor_2_out;

  xor xor_1 (xor_1_out, c3, a3);
  not not_1 (not_1_out, xor_2_out);
  xor xor_2 (xor_2_out, a3, b3);
  and and_1 (O, xor_1_out, not_1_out);
endmodule

module comparador_and (
  input  [3:0] A,
  input  [3:0] B,
  input  Enable_out,
  output [3:0] S
);

  wire [3:0] and_1_out;

  and and_1 (and_1_out[0], A[0], B[0]);
  and and_2 (and_1_out[1], A[1], B[1]);
  and and_3 (and_1_out[2], A[2], B[2]);
  and and_4 (and_1_out[3], A[3], B[3]);
  assign S = Enable_out ? and_1_out : 4'bz;  // Controlled_Buffer controlled_buffer_1
endmodule

module comparador_or (
  input  [3:0] A,
  input  [3:0] B,
  input  Enable_out,
  output [3:0] S
);

  wire [3:0] or_1_out;

  or or_1 (or_1_out[0], A[0], B[0]);
  or or_2 (or_1_out[1], A[1], B[1]);
  or or_3 (or_1_out[2], A[2], B[2]);
  or or_4 (or_1_out[3], A[3], B[3]);
  assign S = Enable_out ? or_1_out : 4'bz;  // Controlled_Buffer controlled_buffer_1
endmodule
